# Fritzing sketch schematics (saved by Fritzing 0.8.7b)
breadboards: 1

parts:
  Componente2 = Arduino Mega 2560 (Rev3)
  LED12 = LED - 5mm [color="Red (633nm)" package="5 mm [THT]"]
  LED13 = LED - 5mm [color="Red (633nm)" package="5 mm [THT]"]
  LED14 = LED - 5mm [color="Red (633nm)" package="5 mm [THT]"]
  LED15 = LED - 5mm [color="Red (633nm)" package="5 mm [THT]"]
  LED16 = LED - 5mm [color="Red (633nm)" package="5 mm [THT]"]
  LED17 = LED - 5mm [color="Red (633nm)" package="5 mm [THT]"]
  LED18 = LED - 5mm [color="Red (633nm)" package="5 mm [THT]"]
  LED19 = LED - 5mm [color="Red (633nm)" package="5 mm [THT]"]
  LED20 = LED - 5mm [color="Red (633nm)" package="5 mm [THT]"]
  LED21 = LED - 5mm [color="Red (633nm)" package="5 mm [THT]"]
  LED23 = LED - 5mm [color="Red (633nm)" package="5 mm [THT]"]
  LED24 = LED - 5mm [color="Red (633nm)" package="5 mm [THT]"]
  R10 = Resistor [tolerance=±5% resistance=220 package=THT]
  S1 = Pushbutton [package="[SMD]"]
  R11 = Resistor [tolerance=±5% resistance=220 package=THT]

nets:
  N1: Componente2.GND, R10.Pin_0
  N2: Componente2.5V, S1.Pin_1, S1.Pin_2
  N3: Componente2.D22, Componente2.D24, Componente2.D26, Componente2.D28, Componente2.D30, Componente2.D32, Componente2.D34, Componente2.D36, Componente2.D38, Componente2.D40, Componente2.D42, Componente2.D44, LED12.cathode, LED12.anode, LED13.cathode, LED13.anode, LED14.cathode, LED14.anode, LED15.cathode, LED15.anode, LED16.cathode, LED16.anode, LED17.cathode, LED17.anode, LED18.cathode, LED18.anode, LED19.cathode, LED19.anode, LED20.cathode, LED20.anode, LED21.cathode, LED21.anode, LED23.cathode, LED23.anode, LED24.cathode, LED24.anode, R10.Pin_1, R11.Pin_0
  N4: Componente2.D46, S1.Pin_3, S1.Pin_4, R11.Pin_1

notes:
  Representacao de keypad 4 x 3:
  ROW3
  ROW2
  ROW1
  ROW0
  COL2
  COL1
  COL0
  Representacao de RC522:
  SDA
  SCK
  MOSI
  MISO
  IRQ
  GND
  RST
  3.3V
  Representacao OLED:
  GND
  VDD
  SDA
  SCK
